# Fritzing sketch Temp-Humid Board BME280 (saved by Fritzing 0.9.3b)
breadboards: 1

parts:
  Raspberry_Pi_3 = Raspberry Pi 3 [part_number=RPI-3-V1.2]
  LCD1 = LCD screen
  LCM1602_IIC1 = LCM1602 IIC [part_number="LCM1602 IIC" chip_label="LCM1602 IIC" package="DIP (Dual Inline) [THT]"]
  GY-BMP280 = GY-BMEP280 Barometric Pressure Sensor - Breakout
  S1 = Pushbutton [package="[SMD]"]

nets:
  N1: Raspberry_Pi_3.GPIO2, LCM1602_IIC1.SDA, GY-BMP280.SDA
  N2: Raspberry_Pi_3.GPIO3, LCM1602_IIC1.SCL, GY-BMP280.SCL
  N3: Raspberry_Pi_3.GPIO17, GY-BMP280.SDO
  N4: Raspberry_Pi_3.GPIO27, S1.Pin_1, S1.Pin_2
  N5: Raspberry_Pi_3.GPIO22, GY-BMP280.CSB
  GND: Raspberry_Pi_3.GND, LCM1602_IIC1.GND, GY-BMP280.GND, S1.Pin_3, S1.Pin_4
  VCC: Raspberry_Pi_3.5V, LCM1602_IIC1.VCC, GY-BMP280.VCC
  VSS: LCD1.VSS, LCM1602_IIC1.VSS
  VDD: LCD1.VDD, LCM1602_IIC1.VDD
  N6: LCD1.V0, LCM1602_IIC1.V0
  N7: LCD1.RS, LCM1602_IIC1.RS
  N8: LCD1.R/W, LCM1602_IIC1.RW
  N9: LCD1.E, LCM1602_IIC1.E
  N10: LCD1.DB0, LCM1602_IIC1.D0
  N11: LCD1.DB1, LCM1602_IIC1.D1
  N12: LCD1.DB2, LCM1602_IIC1.D2
  N13: LCD1.DB3, LCM1602_IIC1.D3
  N14: LCD1.DB4, LCM1602_IIC1.D4
  N15: LCD1.DB5, LCM1602_IIC1.D5
  N16: LCD1.DB6, LCM1602_IIC1.D6
  N17: LCD1.DB7, LCM1602_IIC1.D7
  N18: LCD1.LED+, LCM1602_IIC1.A
  N19: LCD1.LED-, LCM1602_IIC1.K
  N20: LCM1602_IIC1.LED_A, LCM1602_IIC1.LED_B

custom parts:
  LCM1602 IIC: I2C-Module to use a 1602 or 2004 LCD on with the wire.h libory Serial LCD Modul
  GY-BMEP280 Barometric Pressure Sensor - Breakout: The BME280 is a chip which was originally designed for the next generation of smartphones. It is made up of a very accurate pressure sensor and an associated temperature sensor which helps calibrate the pressure readings. And just for fun they threw in a pretty solid humidity sensor in there as well! So with an I2C connection you have access to enough weather data to make some pretty good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
